// Logisim project counter_prototyping.circ as structural Verilog
module main (
  input  in_1,
  input  in_2,
  input  in_3,
  input  in_4,
  input  in_5,
  input  in_6,
  input  in_7,
  input  in_8,
  input  in_9,
  input  in_10,
  output [3:0] out_11,
  output [3:0] out_12,
  output [3:0] out_13
);

  up_down_counter_v1 up_down_counter_v1_1 (.clk(in_1), .rst(in_2), .up_down(in_3), .q(out_11));
  up_down_counter_v2 up_down_counter_v2_1 (.clk(in_4), .rst(in_5), .left_click(in_6), .right_click(in_7), .q(out_12));
  up_down_counter_v3 up_down_counter_v3_1 (.up_clk(in_8), .down_clk(in_9), .reset(in_10), .count_out(out_13));
endmodule

// VHDL entity up_down_counter_v3, as the project stores it:
library ieee;
use ieee.std_logic_1164.all;
use ieee.numeric_std.all;

entity up_down_counter_v3 is
    port (
        up_clk, down_clk, reset : in std_logic;
        count_out : out std_logic_vector(3 downto 0)
    );
end up_down_counter_v3;

architecture behavioral of up_down_counter_v3 is
    signal count : unsigned(3 downto 0);
begin
    process (up_clk, down_clk, reset)
    begin
        if reset = '1' then
            count <= (others => '0');
        elsif rising_edge(up_clk) or falling_edge(up_clk) then 
            count <= count + 1;
            --count_out <= std_logic_vector(count);
        elsif rising_edge(down_clk) or falling_edge(down_clk) then
            count <= count - 1;
            --count_out <= std_logic_vector(count);
        end if;
        
    end process;

    count_out <= std_logic_vector(count);
    
end architecture;

// VHDL entity up_down_counter_v1, as the project stores it:
library IEEE;
use IEEE.STD_LOGIC_1164.ALL;
use IEEE.NUMERIC_STD.ALL;

entity up_down_counter_v1 is
    Port ( clk : in STD_LOGIC;
           rst : in STD_LOGIC;
           up_down : in STD_LOGIC;
           q : out STD_LOGIC_VECTOR (3 downto 0));
end up_down_counter_v1;

architecture Behavioral of up_down_counter_v1 is
    signal count : unsigned(3 downto 0);
begin
    process(clk, rst)
    begin
        if (rst = '1') then
            count <= (others => '0');
        elsif rising_edge(clk) then
            if (up_down = '1') then
                count <= count + 1;
            else
                count <= count - 1;
            end if;
        end if;
        q <= std_logic_vector(count);
    end process;

end Behavioral;

// VHDL entity up_down_counter_v2, as the project stores it:
library IEEE;
use IEEE.STD_LOGIC_1164.ALL;
use IEEE.NUMERIC_STD.ALL;

entity up_down_counter_v2 is
    Port ( clk : in STD_LOGIC;
           rst : in STD_LOGIC;
           left_click : in STD_LOGIC;
           right_click : in STD_LOGIC;
           q : out STD_LOGIC_VECTOR (3 downto 0));
end up_down_counter_v2;

architecture Behavioral of up_down_counter_v2 is
    signal count : unsigned(3 downto 0);
begin
    process(clk, rst, left_click, right_click)
    begin
        if (rst = '1') then
            count <= (others => '0');
        elsif rising_edge(clk) then
            if (left_click = '1') then
                count <= count + 1;
            elsif (right_click = '1') then
                count <= count - 1;
            end if;
        end if;
        q <= std_logic_vector(count);
    end process;

end Behavioral;
